# Fritzing sketch Arc reactor (saved by Fritzing 0.9.3b)

parts:
  Part1 = Arduino Pro Mini (5V)
  Part2 = Bluetooth HC-05 Macho
  U1 = 74HC595 [package="DIP16 [THT]"]
  R3 = Resistor [tolerance=±5% resistance=470 package=THT]
  R4 = Resistor [tolerance=±5% resistance=470 package=THT]
  R2 = Resistor [tolerance=±5% resistance=470 package=THT]
  R1 = Resistor [tolerance=±5% resistance=470 package=THT]
  LED2 = LED - 5mm [color="White (6500K)" package="5 mm [THT]"]
  LED1 = LED - 5mm [color="White (6500K)" package="5 mm [THT]"]
  R5 = Resistor [tolerance=±5% resistance=470 package=THT]
  R6 = Resistor [tolerance=±5% resistance=470 package=THT]
  R7 = Resistor [tolerance=±5% resistance=470 package=THT]
  R8 = Resistor [tolerance=±5% resistance=470 package=THT]
  U2 = 74HC595 [package="DIP16 [THT]"]
  R9 = Resistor [tolerance=±5% resistance=470 package=THT]
  R10 = Resistor [tolerance=±5% resistance=470 package=THT]
  LED10 = LED - 5mm [color="White (6500K)" package="5 mm [THT]"]
  LED9 = LED - 5mm [color="White (6500K)" package="5 mm [THT]"]
  LED3 = LED - 5mm [color="White (6500K)" package="5 mm [THT]"]
  LED4 = LED - 5mm [color="White (6500K)" package="5 mm [THT]"]
  LED5 = LED - 5mm [color="White (6500K)" package="5 mm [THT]"]
  LED6 = LED - 5mm [color="White (6500K)" package="5 mm [THT]"]
  LED7 = LED - 5mm [color="White (6500K)" package="5 mm [THT]"]
  LED8 = LED - 5mm [color="White (6500K)" package="5 mm [THT]"]
  R11 = Resistor [tolerance=±5% resistance=470 package=THT]
  R19 = Resistor [tolerance=±5% resistance=470 package=THT]
  R13 = Resistor [tolerance=±5% resistance=470 package=THT]
  R15 = Resistor [tolerance=±5% resistance=470 package=THT]
  R17 = Resistor [tolerance=±5% resistance=470 package=THT]
  R16 = Resistor [tolerance=±5% resistance=470 package=THT]
  R18 = Resistor [tolerance=±5% resistance=470 package=THT]
  R14 = Resistor [tolerance=±5% resistance=470 package=THT]
  R12 = Resistor [tolerance=±5% resistance=470 package=THT]
  LED13 = LED - 5mm [color="White (6500K)" package="5 mm [THT]"]
  LED14 = LED - 5mm [color="White (6500K)" package="5 mm [THT]"]
  LED19 = LED - 5mm [color="White (6500K)" package="5 mm [THT]"]
  LED17 = LED - 5mm [color="White (6500K)" package="5 mm [THT]"]
  LED16 = LED - 5mm [color="White (6500K)" package="5 mm [THT]"]
  LED18 = LED - 5mm [color="White (6500K)" package="5 mm [THT]"]
  LED12 = LED - 5mm [color="White (6500K)" package="5 mm [THT]"]
  LED15 = LED - 5mm [color="White (6500K)" package="5 mm [THT]"]
  LED11 = LED - 5mm [color="White (6500K)" package="5 mm [THT]"]

nets:
  N1: Part1.TXO, Part2.RXD
  N2: Part1.RXI, Part2.TXD
  VCC: Part1.VCC, Part2.VCC, U1.MR, U1.VCC, U2.MR, U2.VCC
  GND: Part1.GND, Part2.GND, U1.GND, U1.OE, LED2.cathode, LED1.cathode, U2.GND, U2.OE, LED10.cathode, LED9.cathode, LED3.cathode, LED4.cathode, LED5.cathode, LED6.cathode, LED7.cathode, LED8.cathode, LED13.cathode, LED14.cathode, LED19.cathode, LED17.cathode, LED16.cathode, LED18.cathode, LED12.cathode, LED15.cathode, LED11.cathode
  N3: Part1.MOSI, R17.Pin_1, R16.Pin_1
  N4: Part1.D10, R11.Pin_1
  N5: Part1.D9, R19.Pin_1, R18.Pin_1
  N6: Part1.D6, R13.Pin_1, R12.Pin_1
  N7: Part1.D5, R15.Pin_1, R14.Pin_1
  N8: Part1.D4, U1.SH_CP, U2.SH_CP
  N9: Part1.D3, U1.ST_CP, U2.ST_CP
  N10: Part1.D2, U1.DS
  N11: U1.Q1, R2.Pin_1
  N12: U1.Q2, R3.Pin_1
  N13: U1.Q3, R4.Pin_1
  N14: U1.Q4, R5.Pin_1
  N15: U1.Q5, R6.Pin_1
  N16: U1.Q6, R7.Pin_1
  N17: U1.Q7, R8.Pin_1
  N18: U1.Q7', U2.DS
  N19: U1.Q0, R1.Pin_1
  N20: R3.Pin_0, LED3.anode
  N21: R4.Pin_0, LED4.anode
  N22: R2.Pin_0, LED2.anode
  N23: R1.Pin_0, LED1.anode
  N24: R5.Pin_0, LED5.anode
  N25: R6.Pin_0, LED6.anode
  N26: R7.Pin_0, LED7.anode
  N27: R8.Pin_0, LED8.anode
  N28: U2.Q1, R10.Pin_1
  N29: U2.Q0, R9.Pin_1
  N30: R9.Pin_0, LED9.anode
  N31: R10.Pin_0, LED10.anode
  N32: R11.Pin_0, LED11.anode
  N33: R19.Pin_0, LED19.anode
  N34: R13.Pin_0, LED13.anode
  N35: R15.Pin_0, LED15.anode
  N36: R17.Pin_0, LED17.anode
  N37: R16.Pin_0, LED16.anode
  N38: R18.Pin_0, LED18.anode
  N39: R14.Pin_0, LED14.anode
  N40: R12.Pin_0, LED12.anode
